// Logisim project 1.Construa uma memória RAM, com a memória presente no Logisim, com 4 bits de endereços e 8 bits de dados com entrada e saída de dados separadas..circ as structural Verilog: 1 circuit, main circuit main
module main (
  input  [3:0] \Endereços ,
  input  [7:0] Entrada_de_dados,
  input  Load,
  input  Clock,
  input  Select,
  input  Store,
  output [7:0] \Saída_de_dados 
);

  RAM #(.addrWidth(4), .bus("separate")) ram_1 (
    .addr(\Endereços ), .din(Entrada_de_dados), .data(\Saída_de_dados ), .str(Store), .sel(Select),
    .clk(Clock), .ld(Load));  // open: clr

  // Notes on the sheet:
  //   Mateus
endmodule
